// Logisim project schema logique 4 capteurs.circ as structural Verilog: 1 circuit, main circuit main
module main (
  input  Gauche,
  input  Millieu_gauche,
  input  Millieu_droit,
  input  Droit,
  output out_5
);

  wire and_1_out, and_2_out, and_3_out, and_4_out, and_5_out, not_1_out, not_2_out, not_3_out, not_4_out,
       or_1_out, or_2_out, or_4_out;

  not not_1 (not_1_out, Gauche);
  not not_2 (not_2_out, Millieu_gauche);
  and and_1 (and_1_out, Droit, Millieu_droit);
  and and_2 (and_2_out, not_2_out, not_1_out);
  or or_1 (or_1_out, and_1_out, Millieu_droit);
  not not_3 (not_3_out, Millieu_droit);
  not not_4 (not_4_out, Droit);
  and and_3 (and_3_out, or_1_out, and_2_out);
  or or_2 (or_2_out, and_3_out, not_3_out);
  buf and_4 (and_4_out, not_4_out);  // AND_Gate
  and and_5 (and_5_out, and_4_out, Millieu_gauche, Gauche);
  or or_3 (out_5, or_2_out, or_4_out);
  or or_4 (or_4_out, and_5_out, Millieu_gauche);
endmodule
