// Logisim project schéma logique.circ as structural Verilog: 1 circuit, main circuit main
module main (
  input  A,
  input  B,
  input  C,
  output A_B___B_C___B
);

  wire and_1_out, and_2_out;

  and and_1 (and_1_out, A, B);
  and and_2 (and_2_out, B, C);
  or or_1 (A_B___B_C___B, and_1_out, B, and_2_out);

  // Notes on the sheet:
  //   capteur 1 gauche
  //   capteur 2 centre
  //   capteur 3 droit
  //   A.B
  //   B+C
endmodule
