// Logisim project schéma logique pour 3 capteurs.circ as structural Verilog: 1 circuit, main circuit main
module main (
  input  nA,
  input  C,
  input  B,
  input  A,
  input  nC,
  output out_6
);

  wire and_1_out, and_2_out, not_1_out, not_2_out;

  not not_1 (not_1_out, nA);
  not not_2 (not_2_out, nC);
  and and_1 (and_1_out, not_1_out, not_1_out, C);
  and and_2 (and_2_out, A, not_2_out);
  or or_1 (out_6, and_1_out, B, and_2_out);

  // Notes on the sheet:
  //   /A.C
  //   B
  //   A./C
  //   /A.C + B + A./C
endmodule
