// Logisim project schéma logique pour 4 capteurs.circ as structural Verilog: 1 circuit, main circuit main
module main (
  input  nA,
  input  nB,
  input  nC,
  input  nD,
  input  A,
  input  B,
  input  C,
  input  D,
  output out_9
);

  wire and_1_out, and_2_out, and_3_out, not_1_out, not_2_out, not_3_out, not_4_out;

  not not_1 (not_1_out, nA);
  not not_2 (not_2_out, nB);
  not not_3 (not_3_out, nC);
  not not_4 (not_4_out, nD);
  and and_1 (and_1_out, not_1_out, not_2_out);
  and and_2 (and_2_out, not_3_out, not_4_out);
  and and_3 (and_3_out, A, B, C, D);
  or or_1 (out_9, and_1_out, and_2_out, and_3_out);

  // Notes on the sheet:
  //   /A./B
  //   /C./D
  //   A.B.C.D
  //   /A./B + /C./D + ABCD
endmodule
