// Logisim project schema logique.circ as structural Verilog: 1 circuit, main circuit main
module main (
  input  G,
  input  M,
  input  D,
  output S
);

  wire and_1_out, not_1_out, xor_1_out;

  not not_1 (not_1_out, G);
  and and_1 (and_1_out, not_1_out, M);
  xor xor_1 (xor_1_out, G, D);
  or or_1 (S, and_1_out, xor_1_out);
endmodule
